# Fritzing sketch WiringSketch-direct3.3 (saved by Fritzing 0.9.2b)
circuit board: 6.96188cm x 5.55592cm
breadboards: 1

parts:
  Часть1 = Arduino Uno (Rev3)
  VCC1 = Battery
  J1 = Basic Servo
  U2 = ESP8266 WiFi Module [part_number=ESP8266]
  ULN2803a = ULN2803A [package=THT]
  U3 = SWITCH-SPST-2 [package=switch-spst-vertical]
  R-MOTOR = 28BYJ-48 Stepper Motor
  L-MOTOR = 28BYJ-48 Stepper Motor

nets:
  N1: Часть1.D8, ULN2803a.In_5
  N2: Часть1.D9_PWM, ULN2803a.In_6
  N3: Часть1.D10_PWM/SS, ULN2803a.In_7
  N4: Часть1.D11_PWM/MOSI, ULN2803a.In_8
  N5: Часть1.D12/MISO, J1.pulse
  GND: Часть1.GND, VCC1.-, J1.gnd, U2.GND, ULN2803a.0V
  N6: Часть1.D2, ULN2803a.In_1
  N7: Часть1.D3_PWM, ULN2803a.In_2
  N8: Часть1.D4, ULN2803a.In_3
  N9: Часть1.D5_PWM, ULN2803a.In_4
  N10: Часть1.D6_PWM, U2.TXD
  N11: Часть1.D7, U2.RXD
  3V3: Часть1.3V3, U2.VCC, U2.CH_PD
  5V: Часть1.5V, J1.vcc, ULN2803a.COM_-_Common, U3.P, R-MOTOR.RED, L-MOTOR.RED
  N12: VCC1.+, U3.O
  N13: ULN2803a.Out_8, R-MOTOR.ORANGE
  N14: ULN2803a.Out_7, R-MOTOR.YELLOW
  N15: ULN2803a.Out_6, R-MOTOR.PINK
  N16: ULN2803a.Out_5, R-MOTOR.BLUE
  N17: ULN2803a.Out_4, L-MOTOR.BLUE
  N18: ULN2803a.Out_3, L-MOTOR.PINK
  N19: ULN2803a.Out_2, L-MOTOR.YELLOW
  N20: ULN2803a.Out_1, L-MOTOR.ORANGE

notes:
  -
  +
  _/_

custom parts:
  ESP8266 WiFi Module: Generic WiFi Module based on the ESP8266 with onboard PCB antenna and UART communications
  28BYJ-48 Stepper Motor: 28BYJ-48 gear-reduction stepper motor (small)
